// Digital circuit 5.2 ex2.dig as structural Verilog
module _5_2_ex2 (
  input  clk
);

  wire A_q, B_nq, B_q, O_a, O_b, O_c, O_d, O_e, O_f, O_g, O_h, xor_1_out;

  xor xor_1 (xor_1_out, A_q, B_q);
  D_FF A (.D(xor_1_out), .C(clk), .Q(A_q));  // open: nQ
  D_FF B (.D(B_nq), .C(clk), .Q(B_q), .nQ(B_nq));
  _7_segment_driver O (
    .I3(1'b0), .I2(1'b0), .I1(A_q), .I0(B_q), .A(O_a), .B(O_b), .C(O_c), .D(O_d), .E(O_e), .F(O_f), .G(O_g),
    .H(O_h));
  Seven_Seg seven_seg_1 (.a(O_a), .b(O_b), .c(O_c), .d(O_d), .e(O_e), .f(O_f), .g(O_g), .dp(O_h));

  // Notes on the sheet:
  //   A
  //   E
  //   F
  //   D
  //   C
  //   B
  //   G
  //   H
endmodule
