// Digital circuit 7-segment driver.dig as structural Verilog
module _7_segment_driver (
  input  I3,
  input  I2,
  input  I1,
  input  I0,
  output A,
  output B,
  output C,
  output D,
  output E,
  output F,
  output G,
  output H
);

  wire and_1_out, and_2_out, and_3_out, and_4_out, and_5_out, and_6_out, and_7_out, and_8_out, and_9_out,
       and_10_out, and_11_out, and_12_out, and_13_out, and_14_out, and_15_out, and_16_out, not_1_out,
       not_2_out, not_3_out, not_4_out;

  not not_1 (not_1_out, I3);
  not not_2 (not_2_out, I0);
  not not_3 (not_3_out, I2);
  not not_4 (not_4_out, I1);
  and and_1 (and_1_out, not_3_out, not_2_out);
  and and_2 (and_2_out, not_2_out, not_3_out);
  and and_3 (and_3_out, I1, not_2_out);
  and and_4 (and_4_out, I2, not_2_out);
  and and_5 (and_5_out, not_4_out, not_2_out);
  and and_6 (and_6_out, I0, I2);
  and and_7 (and_7_out, I2, not_4_out);
  or or_1 (E, and_3_out, and_1_out);
  or or_2 (A, and_2_out, and_6_out, I1, I3);
  or or_3 (F, I3, and_7_out, and_4_out, and_5_out);
  and and_8 (and_8_out, I2, not_4_out);
  and and_9 (and_9_out, not_1_out, not_3_out, I1);
  and and_10 (and_10_out, not_2_out, I1);
  and and_11 (and_11_out, I0, I1);
  and and_12 (and_12_out, not_2_out, not_4_out);
  and and_13 (and_13_out, I1, not_2_out);
  and and_14 (and_14_out, I0, not_4_out, I2);
  or or_4 (G, I3, and_13_out, and_8_out, and_9_out);
  and and_15 (and_15_out, I1, not_3_out, not_1_out);
  or or_5 (B, and_11_out, and_12_out, not_3_out, I3);
  and and_16 (and_16_out, not_2_out, not_3_out);
  or or_6 (C, not_4_out, I0, I2, I3);
  or or_7 (D, and_14_out, and_15_out, and_10_out, and_16_out, I3);

  assign H = 1'b0;
endmodule
