// Digital circuit C M13T.dig as structural Verilog
module C_M13T (
  input  En,
  input  W,
  input  X,
  input  Y,
  input  Z,
  output A,
  output B,
  output C,
  output D,
  output E,
  output F,
  output G,
  output H
);

  wire and_1_out, and_2_out, and_5_out, and_6_out, and_7_out, and_8_out, and_9_out, and_10_out, and_11_out,
       and_12_out, and_13_out, and_14_out, and_15_out, and_16_out, and_17_out, and_18_out, and_19_out,
       and_20_out, and_21_out, and_22_out, and_23_out, and_24_out, and_25_out, and_26_out, not_1_out,
       not_2_out, not_3_out, not_4_out;

  and and_1 (and_1_out, W, En);
  and and_2 (and_2_out, X, En);
  and and_3 (G, Y, En);
  and and_4 (H, Z, En);
  not not_1 (not_1_out, and_1_out);
  not not_2 (not_2_out, and_2_out);
  not not_3 (not_3_out, G);
  not not_4 (not_4_out, H);
  and and_5 (and_5_out, and_2_out, and_1_out);
  and and_6 (and_6_out, G, and_1_out);
  or or_1 (A, and_6_out, and_5_out);
  and and_7 (and_7_out, H, and_2_out, not_1_out);
  and and_8 (and_8_out, G, and_2_out, not_1_out);
  or or_2 (B, and_10_out, and_9_out, and_8_out, and_7_out);
  and and_9 (and_9_out, H, G, and_2_out);
  and and_10 (and_10_out, not_3_out, not_2_out, and_1_out);
  and and_11 (and_11_out, H, not_3_out, and_1_out);
  and and_12 (and_12_out, not_3_out, not_2_out, and_1_out);
  and and_13 (and_13_out, not_4_out, not_3_out, and_2_out, not_1_out);
  or or_3 (C, and_15_out, and_14_out, and_13_out, and_12_out, and_11_out);
  and and_14 (and_14_out, not_4_out, G, and_2_out, and_1_out);
  and and_15 (and_15_out, H, G, not_2_out, not_1_out);
  and and_16 (and_16_out, not_4_out, not_3_out, and_2_out);
  and and_17 (and_17_out, H, not_3_out, not_2_out, and_1_out);
  and and_18 (and_18_out, not_4_out, G, and_2_out, and_1_out);
  or or_4 (D, and_20_out, and_19_out, and_18_out, and_17_out, and_16_out);
  and and_19 (and_19_out, H, G, and_2_out, not_1_out);
  and and_20 (and_20_out, not_4_out, G, not_2_out, not_1_out);
  and and_21 (and_21_out, not_4_out, G, not_1_out);
  and and_22 (and_22_out, H, G, not_2_out, and_1_out);
  and and_23 (and_23_out, not_4_out, not_3_out, and_1_out);
  and and_24 (and_24_out, not_3_out, and_2_out, and_1_out);
  or or_5 (E, and_26_out, and_25_out, and_24_out, and_23_out, and_22_out, and_21_out);
  and and_25 (and_25_out, H, not_3_out, not_2_out, not_1_out);
  and and_26 (and_26_out, G, and_2_out, not_1_out);
  xor xor_1 (F, H, and_2_out);
endmodule
