// Digital circuit C M1T.dig as structural Verilog
module C_M1T (
  input  En,
  input  W,
  input  X,
  input  Y,
  input  Z,
  output A,
  output B,
  output C,
  output D,
  output E,
  output F,
  output G,
  output H
);

  wire not_1_out, not_2_out, not_3_out, not_4_out;

  and and_1 (E, W, En);
  and and_2 (F, X, En);
  and and_3 (G, Y, En);
  and and_4 (H, Z, En);
  not not_1 (not_1_out, E);
  not not_2 (not_2_out, F);
  not not_3 (not_3_out, G);
  not not_4 (not_4_out, H);

  assign A = 1'b0;
  assign B = 1'b0;
  assign C = 1'b0;
  assign D = 1'b0;
endmodule
