// Digital circuit C M2T.dig as structural Verilog
module C_M2T (
  input  En,
  input  W,
  input  X,
  input  Y,
  input  Z,
  output A,
  output B,
  output C,
  output D,
  output E,
  output F,
  output G,
  output H
);

  wire not_1_out, not_2_out, not_3_out, not_4_out;

  and and_1 (D, W, En);
  and and_2 (E, X, En);
  and and_3 (F, Y, En);
  and and_4 (G, Z, En);
  not not_1 (not_1_out, D);
  not not_2 (not_2_out, E);
  not not_3 (not_3_out, F);
  not not_4 (not_4_out, G);

  assign A = 1'b0;
  assign B = 1'b0;
  assign C = 1'b0;
  assign H = 1'b0;
endmodule
