// Digital circuit C M4T.dig as structural Verilog
module C_M4T (
  input  EN,
  input  W,
  input  X,
  input  Y,
  input  Z,
  output A,
  output B,
  output C,
  output D,
  output E,
  output F,
  output G,
  output H
);

  wire not_1_out, not_2_out, not_3_out, not_4_out;

  and and_1 (C, W, EN);
  and and_2 (D, X, EN);
  and and_3 (E, Y, EN);
  and and_4 (F, Z, EN);
  not not_1 (not_1_out, C);
  not not_2 (not_2_out, D);
  not not_3 (not_3_out, E);
  not not_4 (not_4_out, F);

  assign A = 1'b0;
  assign B = 1'b0;
  assign G = 1'b0;
  assign H = 1'b0;
endmodule
