// Digital circuit C M5T.dig as structural Verilog
module C_M5T (
  input  En,
  input  W,
  input  X,
  input  Y,
  input  Z,
  output O0,
  output _01,
  output O2,
  output O3,
  output O4,
  output O5,
  output O6,
  output O7
);

  wire and_1_out, and_2_out, and_5_out, and_6_out, and_7_out, and_8_out, and_9_out, and_10_out, and_11_out,
       and_12_out, and_13_out, and_14_out, and_15_out, and_16_out, and_17_out, and_18_out, and_19_out,
       not_1_out, not_2_out, not_3_out, not_4_out;

  and and_1 (and_1_out, W, En);
  and and_2 (and_2_out, X, En);
  and and_3 (O6, Y, En);
  and and_4 (O7, Z, En);
  not not_1 (not_1_out, and_1_out);
  not not_2 (not_2_out, and_2_out);
  not not_3 (not_3_out, O6);
  not not_4 (not_4_out, O7);
  and and_5 (and_5_out, O7, and_2_out, and_1_out);
  and and_6 (and_6_out, O6, and_2_out, and_1_out);
  or or_1 (_01, and_6_out, and_5_out);
  and and_7 (and_7_out, not_2_out, and_1_out);
  and and_8 (and_8_out, not_4_out, not_3_out, and_1_out);
  or or_2 (O2, and_9_out, and_8_out, and_7_out);
  and and_9 (and_9_out, O7, O6, and_2_out, not_1_out);
  and and_10 (and_10_out, not_3_out, and_2_out, not_1_out);
  and and_11 (and_11_out, not_4_out, not_3_out, and_2_out);
  or or_3 (O3, and_13_out, and_12_out, and_11_out, and_10_out);
  and and_12 (and_12_out, not_4_out, and_2_out, not_1_out);
  and and_13 (and_13_out, O6, not_2_out, and_1_out);
  and and_14 (and_14_out, O6, not_2_out, not_1_out);
  and and_15 (and_15_out, not_4_out, O6, not_1_out);
  and and_16 (and_16_out, not_3_out, not_2_out, and_1_out);
  and and_17 (and_17_out, not_4_out, not_3_out, and_1_out);
  or or_4 (O4, and_19_out, and_18_out, and_17_out, and_16_out, and_15_out, and_14_out);
  and and_18 (and_18_out, O7, not_3_out, and_2_out, not_1_out);
  and and_19 (and_19_out, O7, O6, and_2_out, and_1_out);
  xor xor_1 (O5, O7, and_2_out);

  assign O0 = 1'b0;
endmodule
