// Digital circuit C M8T.dig as structural Verilog
module C_M8T (
  input  EN,
  input  W,
  input  X,
  input  Y,
  input  Z,
  output A,
  output B,
  output C,
  output D,
  output E,
  output F,
  output G,
  output H
);

  wire not_1_out, not_2_out, not_3_out, not_4_out;

  and and_1 (B, W, EN);
  and and_2 (C, X, EN);
  and and_3 (D, Y, EN);
  and and_4 (E, Z, EN);
  not not_1 (not_1_out, B);
  not not_2 (not_2_out, C);
  not not_3 (not_3_out, D);
  not not_4 (not_4_out, E);

  assign A = 1'b0;
  assign F = 1'b0;
  assign G = 1'b0;
  assign H = 1'b0;
endmodule
