// Digital circuit C M9T.dig as structural Verilog
module C_M9T (
  input  En,
  input  W,
  input  X,
  input  Y,
  input  Z,
  output A,
  output B,
  output C,
  output D,
  output E,
  output F,
  output G,
  output H
);

  wire and_1_out, and_6_out, and_7_out, and_8_out, and_9_out, and_10_out, and_11_out, and_12_out, and_13_out,
       and_14_out, and_15_out, and_16_out, and_17_out, not_1_out, not_2_out, not_3_out, not_4_out;

  and and_1 (and_1_out, W, En);
  and and_2 (F, X, En);
  and and_3 (G, Y, En);
  and and_4 (H, Z, En);
  not not_1 (not_1_out, and_1_out);
  not not_2 (not_2_out, F);
  not not_3 (not_3_out, G);
  not not_4 (not_4_out, H);
  and and_5 (A, H, G, F, and_1_out);
  and and_6 (and_6_out, not_2_out, and_1_out);
  and and_7 (and_7_out, not_3_out, and_1_out);
  or or_1 (B, and_8_out, and_7_out, and_6_out);
  and and_8 (and_8_out, not_4_out, and_1_out);
  and and_9 (and_9_out, F, not_1_out);
  and and_10 (and_10_out, not_3_out, F);
  and and_11 (and_11_out, not_4_out, G, F);
  or or_2 (C, and_12_out, and_11_out, and_10_out, and_9_out);
  and and_12 (and_12_out, H, G, not_2_out, and_1_out);
  and and_13 (and_13_out, G, not_1_out);
  and and_14 (and_14_out, not_4_out, G);
  or or_3 (D, and_15_out, and_14_out, and_13_out);
  and and_15 (and_15_out, H, not_3_out, and_1_out);
  and and_16 (and_16_out, H, not_1_out);
  or or_4 (E, and_17_out, and_16_out);
  and and_17 (and_17_out, not_4_out, and_1_out);
endmodule
