// Digital circuit D M15T.dig as structural Verilog
module D_M15T (
  input  En,
  input  Z,
  input  Y,
  input  X,
  input  W,
  output A,
  output B,
  output C,
  output D,
  output E,
  output F,
  output G,
  output H
);

  wire decoder_1_out_0, decoder_1_out_1, decoder_1_out_2, decoder_1_out_3, decoder_1_out_4, decoder_1_out_5,
       decoder_1_out_6, decoder_1_out_7, decoder_1_out_8, decoder_1_out_9, decoder_1_out_10,
       decoder_1_out_11, decoder_1_out_12, decoder_1_out_13, decoder_1_out_14, decoder_1_out_15;
  wire [3:0] and_1_out;

  and and_1 (and_1_out[0], Z, En);
  and and_2 (and_1_out[1], Y, En);
  and and_3 (and_1_out[2], X, En);
  and and_4 (and_1_out[3], W, En);
  Decoder #(.Selector_Bits(4)) decoder_1 (
    .sel(and_1_out), .out_0(decoder_1_out_0), .out_1(decoder_1_out_1), .out_2(decoder_1_out_2),
    .out_3(decoder_1_out_3), .out_4(decoder_1_out_4), .out_5(decoder_1_out_5), .out_6(decoder_1_out_6),
    .out_7(decoder_1_out_7), .out_8(decoder_1_out_8), .out_9(decoder_1_out_9), .out_10(decoder_1_out_10),
    .out_11(decoder_1_out_11), .out_12(decoder_1_out_12), .out_13(decoder_1_out_13),
    .out_14(decoder_1_out_14), .out_15(decoder_1_out_15));
  or or_1 (A, decoder_1_out_9, decoder_1_out_10, decoder_1_out_11, decoder_1_out_12, decoder_1_out_13, decoder_1_out_14, decoder_1_out_15);
  or or_2 (B, decoder_1_out_5, decoder_1_out_6, decoder_1_out_7, decoder_1_out_8, decoder_1_out_13, decoder_1_out_14, decoder_1_out_15);
  or or_3 (C, decoder_1_out_3, decoder_1_out_4, decoder_1_out_7, decoder_1_out_8, decoder_1_out_11, decoder_1_out_12, decoder_1_out_15);
  or or_4 (D, decoder_1_out_2, decoder_1_out_4, decoder_1_out_6, decoder_1_out_8, decoder_1_out_10, decoder_1_out_12, decoder_1_out_14);
  or or_5 (E, decoder_1_out_1, decoder_1_out_2, decoder_1_out_3, decoder_1_out_4, decoder_1_out_5, decoder_1_out_6, decoder_1_out_7, decoder_1_out_8);
  or or_6 (F, decoder_1_out_1, decoder_1_out_2, decoder_1_out_3, decoder_1_out_4, decoder_1_out_9, decoder_1_out_10, decoder_1_out_11, decoder_1_out_12);
  or or_7 (G, decoder_1_out_1, decoder_1_out_2, decoder_1_out_5, decoder_1_out_6, decoder_1_out_9, decoder_1_out_10, decoder_1_out_13, decoder_1_out_14);
  or or_8 (H, decoder_1_out_1, decoder_1_out_3, decoder_1_out_5, decoder_1_out_7, decoder_1_out_9, decoder_1_out_11, decoder_1_out_13, decoder_1_out_15);
endmodule
