// Digital circuit D M9T.dig as structural Verilog
module D_M9T (
  input  EN,
  input  W,
  input  X,
  input  Y,
  input  Z,
  output A,
  output B,
  output C,
  output D,
  output E,
  output F,
  output G,
  output H
);

  wire decoder_1_out_0, decoder_1_out_1, decoder_1_out_2, decoder_1_out_3, decoder_1_out_4, decoder_1_out_5,
       decoder_1_out_6, decoder_1_out_7, decoder_1_out_8, decoder_1_out_9, decoder_1_out_10,
       decoder_1_out_11, decoder_1_out_12, decoder_1_out_13, decoder_1_out_14;
  wire [3:0] and_4_out;

  and and_1 (and_4_out[0], Z, EN);
  and and_2 (and_4_out[1], Y, EN);
  and and_3 (and_4_out[2], X, EN);
  and and_4 (and_4_out[3], W, EN);
  Decoder #(.Selector_Bits(4)) decoder_1 (
    .sel(and_4_out), .out_0(decoder_1_out_0), .out_1(decoder_1_out_1), .out_2(decoder_1_out_2),
    .out_3(decoder_1_out_3), .out_4(decoder_1_out_4), .out_5(decoder_1_out_5), .out_6(decoder_1_out_6),
    .out_7(decoder_1_out_7), .out_8(decoder_1_out_8), .out_9(decoder_1_out_9), .out_10(decoder_1_out_10),
    .out_11(decoder_1_out_11), .out_12(decoder_1_out_12), .out_13(decoder_1_out_13),
    .out_14(decoder_1_out_14), .out_15(A));
  or or_1 (B, decoder_1_out_14, decoder_1_out_13, decoder_1_out_12, decoder_1_out_11, decoder_1_out_10, decoder_1_out_9, decoder_1_out_8);
  or or_2 (C, decoder_1_out_14, decoder_1_out_13, decoder_1_out_12, decoder_1_out_11, decoder_1_out_7, decoder_1_out_6, decoder_1_out_5, decoder_1_out_4);
  or or_3 (D, decoder_1_out_14, decoder_1_out_13, decoder_1_out_10, decoder_1_out_9, decoder_1_out_7, decoder_1_out_6, decoder_1_out_3, decoder_1_out_2);
  or or_4 (E, decoder_1_out_14, decoder_1_out_12, decoder_1_out_10, decoder_1_out_8, decoder_1_out_7, decoder_1_out_5, decoder_1_out_3, decoder_1_out_1);
  or or_5 (F, A, decoder_1_out_14, decoder_1_out_13, decoder_1_out_12, decoder_1_out_7, decoder_1_out_6, decoder_1_out_5, decoder_1_out_4);
  or or_6 (G, A, decoder_1_out_14, decoder_1_out_11, decoder_1_out_10, decoder_1_out_7, decoder_1_out_6, decoder_1_out_3, decoder_1_out_2);
  or or_7 (H, A, decoder_1_out_13, decoder_1_out_11, decoder_1_out_9, decoder_1_out_7, decoder_1_out_5, decoder_1_out_3, decoder_1_out_1);
endmodule
