// Digital circuit DDA 4B.dig as structural Verilog
module DDA_4B (
  input  I0,
  input  I1,
  input  I2,
  input  I3,
  output O0,
  output O1,
  output O2,
  output O3,
  output T0,
  output T1,
  output T2,
  output T3
);

  dabble Z (.I3(1'b0), .I2(I3), .I1(I2), .I0(I1), .O3(T0), .O2(O3), .O1(O2), .O0(O1));

  assign O0 = I0;
  assign T1 = 1'b0;
  assign T2 = 1'b0;
  assign T3 = 1'b0;
endmodule
