// Digital circuit DDA 8B.dig as structural Verilog
module DDA_8B (
  input  I7,
  input  I6,
  input  I5,
  input  I4,
  input  I3,
  input  I2,
  input  I1,
  input  I0,
  output H3,
  output H2,
  output H1,
  output H0,
  output T3,
  output T2,
  output T1,
  output T0,
  output O3,
  output O2,
  output O1,
  output O0
);

  wire T_o0, T_o1, T_o2, T_o3, U_o0, U_o1, U_o2, U_o3, V_o0, V_o1, V_o2, V_o3, W_o0, W_o1, W_o2, X_o0, X_o1,
       X_o2, X_o3;

  dabble T (.I3(1'b0), .I2(I7), .I1(I6), .I0(I5), .O3(T_o3), .O2(T_o2), .O1(T_o1), .O0(T_o0));
  dabble U (.I3(T_o2), .I2(T_o1), .I1(T_o0), .I0(I4), .O3(U_o3), .O2(U_o2), .O1(U_o1), .O0(U_o0));
  dabble V (.I3(U_o2), .I2(U_o1), .I1(U_o0), .I0(I3), .O3(V_o3), .O2(V_o2), .O1(V_o1), .O0(V_o0));
  dabble X (.I3(V_o2), .I2(V_o1), .I1(V_o0), .I0(I2), .O3(X_o3), .O2(X_o2), .O1(X_o1), .O0(X_o0));
  dabble W (.I3(1'b0), .I2(T_o3), .I1(U_o3), .I0(V_o3), .O3(H1), .O2(W_o2), .O1(W_o1), .O0(W_o0));
  dabble Z (.I3(X_o2), .I2(X_o1), .I1(X_o0), .I0(I1), .O3(T0), .O2(O3), .O1(O2), .O0(O1));
  dabble Y (.I3(W_o2), .I2(W_o1), .I1(W_o0), .I0(X_o3), .O3(H0), .O2(T3), .O1(T2), .O0(T1));

  assign H2 = 1'b0;
  assign H3 = 1'b0;
  assign O0 = I0;

  // Notes on the sheet:
  //   (H)
  //   (G)
  //   (F)
  //   (D)
  //   (C)
  //   (B)
  //   (A)
  //   I4 (D)
  //   I7 (A)
  //   I6 (B)
  //   I1 (G)
  //   I2 (F)
  //   I3 (E)
  //   0
  //   I5 (C)
  //   I0 (H)
  //   T3
  //   T2
  //   T1
  //   T0
  //   U3
  //   U2
  //   U1
  //   U0
  //   V3
  //   V2
  //   V1
  //   V0
  //   X3
  //   X2
  //   X1
  //   W3
  //   W2
  //   X0
  //   W1
  //   W0
  //   Z3
  //   Z1
  //   Z0
  //   Y3
  //   Y1
  //   Y0
  //   Z2
  //   Y2
endmodule
