// Digital circuit FA_4B-4B.dig as structural Verilog
module FA_4B_4B (
  input  En,
  input  A0,
  input  A1,
  input  A2,
  input  A3,
  input  B0,
  input  B1,
  input  B2,
  input  B3,
  output S0,
  output S1,
  output S2,
  output S3,
  output C4,
  output S5,
  output S6,
  output S7
);

  wire and_1_out, and_2_out, and_3_out, and_4_out, and_5_out, and_6_out, and_7_out, and_8_out, and_13_out,
       not_1_out, not_2_out, not_3_out, not_4_out, or_1_out, or_2_out, or_3_out, or_4_out, xor_1_out,
       xor_2_out, xor_3_out, xor_4_out, xor_5_out, xor_6_out, xor_7_out, xor_8_out;

  not not_1 (not_1_out, B0);
  not not_2 (not_2_out, B1);
  not not_3 (not_3_out, B2);
  not not_4 (not_4_out, B3);
  xor xor_1 (xor_1_out, A0, not_1_out);
  and and_1 (and_1_out, not_1_out, A0);
  xor xor_2 (xor_2_out, A1, not_2_out);
  and and_2 (and_2_out, not_2_out, A1);
  xor xor_3 (xor_3_out, A2, not_3_out);
  and and_3 (and_3_out, not_3_out, A2);
  xor xor_4 (xor_4_out, A3, not_4_out);
  and and_4 (and_4_out, not_4_out, A3);
  xor xor_5 (xor_5_out, xor_1_out, 1'b1);
  and and_5 (and_5_out, 1'b1, xor_1_out);
  xor xor_6 (xor_6_out, xor_2_out, or_1_out);
  and and_6 (and_6_out, or_1_out, xor_2_out);
  xor xor_7 (xor_7_out, xor_3_out, or_2_out);
  and and_7 (and_7_out, or_2_out, xor_3_out);
  xor xor_8 (xor_8_out, xor_4_out, or_3_out);
  and and_8 (and_8_out, or_3_out, xor_4_out);
  or or_1 (or_1_out, and_5_out, and_1_out);
  or or_2 (or_2_out, and_6_out, and_2_out);
  or or_3 (or_3_out, and_7_out, and_3_out);
  or or_4 (or_4_out, and_8_out, and_4_out);
  and and_9 (S0, xor_5_out, En);
  and and_10 (S1, xor_6_out, En);
  and and_11 (S2, xor_7_out, En);
  and and_12 (S3, xor_8_out, En);
  and and_13 (and_13_out, or_4_out, En);

  assign C4 = 1'b0;
  assign S5 = 1'b0;
  assign S6 = 1'b0;
  assign S7 = 1'b0;
endmodule
