// Digital circuit M M13T.dig as structural Verilog
module M_M13T (
  input  EN,
  input  W,
  input  X,
  input  Y,
  input  Z,
  output A,
  output B,
  output C,
  output D,
  output E,
  output F,
  output G,
  output H
);

  wire [3:0] and_4_out;

  and and_1 (and_4_out[0], Z, EN);
  and and_2 (and_4_out[1], Y, EN);
  and and_3 (and_4_out[2], X, EN);
  and and_4 (and_4_out[3], W, EN);
  Multiplexer #(.Selector_Bits(4)) multiplexer_1 (
    .sel(and_4_out), .in_0(1'b0), .in_1(1'b0), .in_2(1'b0), .in_3(1'b0), .in_4(1'b0), .in_5(1'b0),
    .in_6(1'b0), .in_7(1'b0), .in_8(1'b0), .in_9(1'b0), .in_10(1'b1), .in_11(1'b1), .in_12(1'b1),
    .in_13(1'b1), .in_14(1'b1), .in_15(1'b1), .out(A));
  Multiplexer #(.Selector_Bits(4)) multiplexer_2 (
    .sel(and_4_out), .in_0(1'b0), .in_1(1'b0), .in_2(1'b0), .in_3(1'b0), .in_4(1'b0), .in_5(1'b1),
    .in_6(1'b1), .in_7(1'b1), .in_8(1'b1), .in_9(1'b1), .in_10(1'b0), .in_11(1'b0), .in_12(1'b0),
    .in_13(1'b0), .in_14(1'b0), .in_15(1'b1), .out(B));
  Multiplexer #(.Selector_Bits(4)) multiplexer_3 (
    .sel(and_4_out), .in_0(1'b0), .in_1(1'b0), .in_2(1'b0), .in_3(1'b1), .in_4(1'b1), .in_5(1'b0),
    .in_6(1'b0), .in_7(1'b0), .in_8(1'b1), .in_9(1'b1), .in_10(1'b0), .in_11(1'b0), .in_12(1'b0),
    .in_13(1'b1), .in_14(1'b1), .in_15(1'b0), .out(C));
  Multiplexer #(.Selector_Bits(4)) multiplexer_4 (
    .sel(and_4_out), .in_0(1'b0), .in_1(1'b0), .in_2(1'b1), .in_3(1'b0), .in_4(1'b1), .in_5(1'b0),
    .in_6(1'b0), .in_7(1'b1), .in_8(1'b0), .in_9(1'b1), .in_10(1'b0), .in_11(1'b0), .in_12(1'b1),
    .in_13(1'b0), .in_14(1'b1), .in_15(1'b0), .out(D));
  Multiplexer #(.Selector_Bits(4)) multiplexer_5 (
    .sel(and_4_out), .in_0(1'b0), .in_1(1'b1), .in_2(1'b1), .in_3(1'b0), .in_4(1'b0), .in_5(1'b0),
    .in_6(1'b1), .in_7(1'b1), .in_8(1'b1), .in_9(1'b0), .in_10(1'b0), .in_11(1'b1), .in_12(1'b1),
    .in_13(1'b1), .in_14(1'b0), .in_15(1'b0), .out(E));
  Multiplexer #(.Selector_Bits(4)) multiplexer_6 (
    .sel(and_4_out), .in_0(1'b0), .in_1(1'b1), .in_2(1'b0), .in_3(1'b1), .in_4(1'b1), .in_5(1'b0),
    .in_6(1'b1), .in_7(1'b0), .in_8(1'b0), .in_9(1'b1), .in_10(1'b0), .in_11(1'b1), .in_12(1'b1),
    .in_13(1'b0), .in_14(1'b1), .in_15(1'b0), .out(F));
  Multiplexer #(.Selector_Bits(4)) multiplexer_7 (
    .sel(and_4_out), .in_0(1'b0), .in_1(1'b0), .in_2(1'b1), .in_3(1'b1), .in_4(1'b0), .in_5(1'b0),
    .in_6(1'b1), .in_7(1'b1), .in_8(1'b0), .in_9(1'b0), .in_10(1'b1), .in_11(1'b1), .in_12(1'b0),
    .in_13(1'b0), .in_14(1'b1), .in_15(1'b1), .out(G));
  Multiplexer #(.Selector_Bits(4)) multiplexer_8 (
    .sel(and_4_out), .in_0(1'b0), .in_1(1'b1), .in_2(1'b0), .in_3(1'b1), .in_4(1'b0), .in_5(1'b1),
    .in_6(1'b0), .in_7(1'b1), .in_8(1'b0), .in_9(1'b1), .in_10(1'b0), .in_11(1'b1), .in_12(1'b0),
    .in_13(1'b1), .in_14(1'b0), .in_15(1'b1), .out(H));
endmodule
