// Digital circuit Multiplier (015)C.dig as structural Verilog
module Multiplier__015_C (
  input  En,
  input  A0,
  input  A1,
  input  A2,
  input  A3,
  input  B0,
  input  B1,
  input  B2,
  input  B3,
  output [7:0] F
);

  wire and_5_out, and_6_out, and_7_out, and_8_out, and_9_out, and_10_out, and_11_out, and_12_out, and_13_out,
       and_14_out, and_15_out, and_16_out, and_17_out, and_18_out, and_19_out, and_20_out, not_1_out,
       not_2_out, not_3_out, not_4_out;
  wire [3:0] and_4_out;
  wire [7:0] undriven, undriven_2, undriven_3, undriven_4, undriven_5, undriven_6, undriven_7, undriven_8,
       undriven_9, undriven_10, undriven_11, undriven_12, undriven_13, undriven_14, undriven_15, undriven_16;

  and and_1 (and_4_out[3], A3, En);
  and and_2 (and_4_out[2], A2, En);
  and and_3 (and_4_out[1], A1, En);
  and and_4 (and_4_out[0], A0, En);
  not not_1 (not_1_out, and_4_out[3]);
  not not_2 (not_2_out, and_4_out[2]);
  not not_3 (not_3_out, and_4_out[1]);
  not not_4 (not_4_out, and_4_out[0]);
  and and_5 (and_5_out, not_4_out, not_3_out, not_2_out, not_1_out);
  and and_6 (and_6_out, and_4_out[0], not_3_out, not_2_out, not_1_out);
  and and_7 (and_7_out, not_4_out, and_4_out[1], not_2_out, not_1_out);
  and and_8 (and_8_out, and_4_out[0], and_4_out[1], not_2_out, not_1_out);
  and and_9 (and_9_out, not_4_out, not_3_out, and_4_out[2], not_1_out);
  and and_10 (and_10_out, and_4_out[0], not_3_out, and_4_out[2], not_1_out);
  and and_11 (and_11_out, not_4_out, and_4_out[1], and_4_out[2], not_1_out);
  and and_12 (and_12_out, and_4_out[0], and_4_out[1], and_4_out[2], not_1_out);
  and and_13 (and_13_out, not_4_out, not_3_out, not_2_out, and_4_out[3]);
  and and_14 (and_14_out, and_4_out[0], not_3_out, not_2_out, and_4_out[3]);
  and and_15 (and_15_out, not_4_out, and_4_out[1], not_2_out, and_4_out[3]);
  and and_16 (and_16_out, and_4_out[0], and_4_out[1], not_2_out, and_4_out[3]);
  and and_17 (and_17_out, not_4_out, not_3_out, and_4_out[2], and_4_out[3]);
  and and_18 (and_18_out, and_4_out[0], not_3_out, and_4_out[2], and_4_out[3]);
  and and_19 (and_19_out, not_4_out, and_4_out[1], and_4_out[2], and_4_out[3]);
  and and_20 (and_20_out, and_4_out[0], and_4_out[1], and_4_out[2], and_4_out[3]);
  // C_M2T c_m2t_1: pin names not known; wires that end beside it: B3, B2, B1, B0, and_7_out, B3, B2, B1, B0, B3, B2, B1, B0
  // C_M0T c_m0t_1: pin names not known; wires that end beside it: and_5_out, and_6_out, and_7_out, and_5_out, B3, B2, B1, B0
  // C_M1T c_m1t_1: pin names not known; wires that end beside it: and_6_out, B3, B2, B1, B0
  // C_M3T c_m3t_1: pin names not known; wires that end beside it: and_8_out, and_9_out, and_10_out, and_8_out, B3, B2, B1, B0
  // C_M4T c_m4t_1: pin names not known; wires that end beside it: and_9_out, B3, B2, B1, B0
  // C_M5T c_m5t_1: pin names not known; wires that end beside it: and_10_out, B3, B2, B1, B0, B3, B2, B1, B0
  // C_M6T c_m6t_1: pin names not known; wires that end beside it: and_11_out, and_12_out, and_13_out, and_11_out, B3, B2, B1, B0
  // C_M7T c_m7t_1: pin names not known; wires that end beside it: and_12_out, B3, B2, B1, B0
  // C_M8T c_m8t_1: pin names not known; wires that end beside it: and_13_out, B3, B2, B1, B0, B3, B2, B1, B0
  // C_M10T c_m10t_1: pin names not known; wires that end beside it: and_15_out, B3, B2, B1, B0
  // C_M11T c_m11t_1: pin names not known; wires that end beside it: and_16_out, B3, B2, B1, B0, B3, B2, B1, B0
  // C_M9T c_m9t_1: pin names not known; wires that end beside it: and_14_out, and_15_out, and_16_out, and_14_out, B3, B2, B1, B0
  // C_M14T c_m14t_1: pin names not known; wires that end beside it: and_19_out, B3, B2, B1, B0, B3, B2, B1, B0
  // C_M12T c_m12t_1: pin names not known; wires that end beside it: and_17_out, and_18_out, and_19_out, and_17_out, B3, B2, B1, B0
  // C_M13T c_m13t_1: pin names not known; wires that end beside it: and_18_out, B3, B2, B1, B0
  // C_M15T c_m15t_1: pin names not known; wires that end beside it: and_20_out, and_20_out, B3, B2, B1, B0, B1, B0
  Multiplexer #(.Selector_Bits(4), .Bits(8)) multiplexer_1 (
    .sel(and_4_out), .in_0(undriven), .in_1(undriven_2), .in_2(undriven_3), .in_3(undriven_4),
    .in_4(undriven_5), .in_5(undriven_6), .in_6(undriven_7), .in_7(undriven_8), .in_8(undriven_9),
    .in_9(undriven_10), .in_10(undriven_11), .in_11(undriven_12), .in_12(undriven_13), .in_13(undriven_14),
    .in_14(undriven_15), .in_15(undriven_16), .out(F));

  // Notes on the sheet:
  //   A1
  //   A0
  //   A3
  //   A2
  //   (W)
  //   (X)
  //   (Y)
  //   (Z)
  //   B3
  //   B2
  //   W
  //   X
  //   Y
  //   B1
  //   B0
  //   Z
  //   0
  //   1
  //   2
  //   3
  //   4
  //   5
  //   6
  //   7
  //   8
  //   9
  //   10
  //   11
  //   12
  //   13
  //   14
  //   15
endmodule
