// Digital circuit Multiplier (015)D.dig as structural Verilog
module Multiplier__015_D (
  input  En,
  input  A0,
  input  A1,
  input  A2,
  input  A3,
  input  B0,
  input  B1,
  input  B2,
  input  B3,
  output [7:0] F
);

  wire decoder_1_out_0, decoder_1_out_1, decoder_1_out_2, decoder_1_out_3, decoder_1_out_4, decoder_1_out_5,
       decoder_1_out_6, decoder_1_out_7, decoder_1_out_8, decoder_1_out_9, decoder_1_out_10,
       decoder_1_out_11, decoder_1_out_12, decoder_1_out_13, decoder_1_out_14, decoder_1_out_15;
  wire [3:0] and_4_out;
  wire [7:0] d_m15t_1_h, undriven, undriven_2, undriven_3, undriven_4, undriven_5, undriven_6, undriven_7,
       undriven_8, undriven_9, undriven_10, undriven_11, undriven_12, undriven_13, undriven_14, undriven_15;

  and and_1 (and_4_out[3], A3, En);
  and and_2 (and_4_out[2], A2, En);
  and and_3 (and_4_out[1], A1, En);
  and and_4 (and_4_out[0], A0, En);
  Decoder #(.Selector_Bits(4)) decoder_1 (
    .sel(and_4_out), .out_0(decoder_1_out_0), .out_1(decoder_1_out_1), .out_2(decoder_1_out_2),
    .out_3(decoder_1_out_3), .out_4(decoder_1_out_4), .out_5(decoder_1_out_5), .out_6(decoder_1_out_6),
    .out_7(decoder_1_out_7), .out_8(decoder_1_out_8), .out_9(decoder_1_out_9), .out_10(decoder_1_out_10),
    .out_11(decoder_1_out_11), .out_12(decoder_1_out_12), .out_13(decoder_1_out_13),
    .out_14(decoder_1_out_14), .out_15(decoder_1_out_15));
  // D_M0T d_m0t_1: pin names not known; wires that end beside it: decoder_1_out_0, decoder_1_out_1, decoder_1_out_2, decoder_1_out_0, B3, B2, B1, B0
  // D_M1T d_m1t_1: pin names not known; wires that end beside it: decoder_1_out_1, B3, B2, B1, B0
  // D_M2T d_m2t_1: pin names not known; wires that end beside it: B3, B2, B1, B0, decoder_1_out_2, B3, B2, B1, B0, B3, B2, B1, B0
  // D_M4T d_m4t_1: pin names not known; wires that end beside it: decoder_1_out_4, B3, B2, B1, B0
  // D_M5T d_m5t_1: pin names not known; wires that end beside it: decoder_1_out_5, B3, B2, B1, B0, B3, B2, B1, B0
  // D_M3T d_m3t_1: pin names not known; wires that end beside it: decoder_1_out_3, decoder_1_out_4, decoder_1_out_5, decoder_1_out_3, B3, B2, B1, B0
  // D_M8T d_m8t_1: pin names not known; wires that end beside it: decoder_1_out_8, B3, B2, B1, B0, B3, B2, B1, B0
  // D_M6T d_m6t_1: pin names not known; wires that end beside it: decoder_1_out_6, decoder_1_out_7, decoder_1_out_8, decoder_1_out_6, B3, B2, B1, B0
  // D_M7T d_m7t_1: pin names not known; wires that end beside it: decoder_1_out_7, B3, B2, B1, B0
  // D_M9T d_m9t_1: pin names not known; wires that end beside it: decoder_1_out_9, decoder_1_out_10, decoder_1_out_11, decoder_1_out_9, B3, B2, B1, B0
  // D_M10T d_m10t_1: pin names not known; wires that end beside it: decoder_1_out_10, B3, B2, B1, B0
  // D_M11T d_m11t_1: pin names not known; wires that end beside it: decoder_1_out_11, B3, B2, B1, B0, B3, B2, B1, B0
  // D_M12T d_m12t_1: pin names not known; wires that end beside it: decoder_1_out_12, decoder_1_out_13, decoder_1_out_14, decoder_1_out_12, B3, B2, B1, B0, B0, decoder_1_out_15
  // D_M13T d_m13t_1: pin names not known; wires that end beside it: decoder_1_out_13, B3, B2, B1, B0
  // D_M14T d_m14t_1: pin names not known; wires that end beside it: decoder_1_out_14, B3, B2, B1, B0, B3, B2, B1, B0
  D_M15T d_m15t_1 (
    .En(decoder_1_out_15), .Z(B3), .Y(B2), .X(B1), .W(B0), .A(d_m15t_1_h[7]), .B(d_m15t_1_h[6]),
    .C(d_m15t_1_h[5]), .D(d_m15t_1_h[4]), .E(d_m15t_1_h[3]), .F(d_m15t_1_h[2]), .G(d_m15t_1_h[1]),
    .H(d_m15t_1_h[0]));
  Multiplexer #(.Selector_Bits(4), .Bits(8)) multiplexer_1 (
    .sel(and_4_out), .in_0(undriven_15), .in_1(undriven_14), .in_2(undriven_13), .in_3(undriven_12),
    .in_4(undriven_11), .in_5(undriven_10), .in_6(undriven_9), .in_7(undriven_8), .in_8(undriven_7),
    .in_9(undriven_6), .in_10(undriven_5), .in_11(undriven_4), .in_12(undriven_3), .in_13(undriven_2),
    .in_14(undriven), .in_15(d_m15t_1_h), .out(F));

  // Notes on the sheet:
  //   (W)
  //   (X)
  //   (Y)
  //   (Z)
  //   A2
  //   A1
  //   A0
  //   A3
  //   W
  //   B3
  //   B2
  //   B1
  //   B0
  //   X
  //   Y
  //   Z
  //   0
  //   1
  //   2
  //   3
  //   4
  //   5
  //   6
  //   7
  //   8
  //   9
  //   10
  //   11
  //   12
  //   13
  //   14
  //   15
endmodule
