// Digital circuit OS.dig as structural Verilog
module OS (
  input  [7:0] X,
  input  [7:0] plus,
  input  [7:0] in_3,
  output O7,
  output O6,
  output O5,
  output O4,
  output O3,
  output O2,
  output O1,
  output O0
);

  or or_1 (O0, X[0], plus[0], in_3[0]);
  or or_2 (O1, X[1], plus[1], in_3[1]);
  or or_3 (O2, X[2], plus[2], in_3[2]);
  or or_4 (O3, X[3], plus[3], in_3[3]);
  or or_5 (O4, X[4], plus[4], in_3[4]);
  or or_6 (O5, X[5], plus[5], in_3[5]);
  or or_7 (O6, X[6], plus[6], in_3[6]);
  or or_8 (O7, X[7], plus[7], in_3[7]);
  // Pins of 1 and 8 bits meet at X
  // Pins of 1 and 8 bits meet at plus
  // Pins of 1 and 8 bits meet at in_3
endmodule
