// Digital circuit Project Calculator D.dig as structural Verilog
module Project_Calculator_D (
);

  wire A_o0, A_o1, A_o2, A_o3, A_t0, A_t1, A_t2, A_t3, and_1_out, and_2_out, B_o0, B_o1, B_o2, B_o3, B_t0,
       B_t1, B_t2, B_t3, dda_8b_1_h0, dda_8b_1_h1, dda_8b_1_h2, dda_8b_1_h3, dda_8b_1_o0, dda_8b_1_o1,
       dda_8b_1_o2, dda_8b_1_o3, dda_8b_1_t0, dda_8b_1_t1, dda_8b_1_t2, dda_8b_1_t3, dipswitch_out, H_a, H_b,
       H_c, H_d, H_e, H_f, H_g, H_h, multiplier__015_d_1_p1, multiplier__015_d_1_p2, multiplier__015_d_1_p3,
       multiplier__015_d_1_p4, multiplier__015_d_1_p5, multiplier__015_d_1_p6, multiplier__015_d_1_p7,
       multiplier__015_d_1_p8, multiplier__015_d_1_p9, multiplier__015_d_1_p10, O_a, O_b, O_c, O_d, O_e, O_f,
       O_g, O_h, OA_a, OA_b, OA_c, OA_d, OA_e, OA_f, OA_g, OA_h, OB_a, OB_b, OB_c, OB_d, OB_e, OB_f, OB_g,
       OB_h, or_1_out, os_1_p4, os_1_p5, os_1_p6, os_1_p7, os_1_p8, os_1_p9, os_1_p10, os_1_p11, plus_out,
       T_a, T_b, T_c, T_d, T_e, T_f, T_g, T_h, TA_a, TA_b, TA_c, TA_d, TA_e, TA_f, TA_g, TA_h, TB_a, TB_b,
       TB_c, TB_d, TB_e, TB_f, TB_g, TB_h;
  wire [7:0] fa_4b_4b_1_s0, fa_4b_4b_2_s0;

  or or_1 (or_1_out, dipswitch_out, plus_out, multiplier__015_d_1_p1);
  // Multiplier__015_D multiplier__015_d_1: pin names not known; wires that end beside it: multiplier__015_d_1_p1, multiplier__015_d_1_p2, multiplier__015_d_1_p3, multiplier__015_d_1_p4, multiplier__015_d_1_p5, multiplier__015_d_1_p6, multiplier__015_d_1_p7, multiplier__015_d_1_p8, multiplier__015_d_1_p9, multiplier__015_d_1_p10
  FA_4B_4B fa_4b_4b_1 (
    .En(plus_out), .A0(multiplier__015_d_1_p2), .A1(multiplier__015_d_1_p3), .A2(multiplier__015_d_1_p4),
    .A3(multiplier__015_d_1_p5), .B0(multiplier__015_d_1_p6), .B1(multiplier__015_d_1_p7),
    .B2(multiplier__015_d_1_p8), .B3(multiplier__015_d_1_p9), .S0(fa_4b_4b_1_s0[0]), .S1(fa_4b_4b_1_s0[1]),
    .S2(fa_4b_4b_1_s0[2]), .S3(fa_4b_4b_1_s0[3]), .C4(fa_4b_4b_1_s0[4]), .S5(fa_4b_4b_1_s0[5]),
    .S6(fa_4b_4b_1_s0[6]), .S7(fa_4b_4b_1_s0[7]));
  FA_4B_4B fa_4b_4b_2 (
    .En(dipswitch_out), .A0(multiplier__015_d_1_p2), .A1(multiplier__015_d_1_p3),
    .A2(multiplier__015_d_1_p4), .A3(multiplier__015_d_1_p5), .B0(multiplier__015_d_1_p6),
    .B1(multiplier__015_d_1_p7), .B2(multiplier__015_d_1_p8), .B3(multiplier__015_d_1_p9),
    .S0(fa_4b_4b_2_s0[0]), .S1(fa_4b_4b_2_s0[1]), .S2(fa_4b_4b_2_s0[2]), .S3(fa_4b_4b_2_s0[3]),
    .C4(fa_4b_4b_2_s0[4]), .S5(fa_4b_4b_2_s0[5]), .S6(fa_4b_4b_2_s0[6]), .S7(fa_4b_4b_2_s0[7]));
  DDA_4B A (
    .I0(multiplier__015_d_1_p2), .I1(multiplier__015_d_1_p3), .I2(multiplier__015_d_1_p4),
    .I3(multiplier__015_d_1_p5), .O0(A_o0), .O1(A_o1), .O2(A_o2), .O3(A_o3), .T0(A_t0), .T1(A_t1), .T2(A_t2),
    .T3(A_t3));
  and and_1 (and_1_out, 1'b1, or_1_out);
  and and_2 (and_2_out, 1'b1, or_1_out);
  _7_segment_driver TA (
    .I3(A_t3), .I2(A_t2), .I1(A_t1), .I0(A_t0), .A(TA_a), .B(TA_b), .C(TA_c), .D(TA_d), .E(TA_e), .F(TA_f),
    .G(TA_g), .H(TA_h));
  Seven_Seg seven_seg_1 (.a(TA_a), .b(TA_b), .c(TA_c), .d(TA_d), .e(TA_e), .f(TA_f), .g(TA_g), .dp(TA_h));
  _7_segment_driver OA (
    .I3(A_o3), .I2(A_o2), .I1(A_o1), .I0(A_o0), .A(OA_a), .B(OA_b), .C(OA_c), .D(OA_d), .E(OA_e), .F(OA_f),
    .G(OA_g), .H(OA_h));
  Seven_Seg seven_seg_2 (.a(OA_a), .b(OA_b), .c(OA_c), .d(OA_d), .e(OA_e), .f(OA_f), .g(OA_g), .dp(OA_h));
  DipSwitch A0 (.out(multiplier__015_d_1_p2));
  DipSwitch A1 (.out(multiplier__015_d_1_p3));
  DipSwitch A2 (.out(multiplier__015_d_1_p4));
  DipSwitch A3 (.out(multiplier__015_d_1_p5));
  DipSwitch X (.out(multiplier__015_d_1_p1));
  DipSwitch plus (.out(plus_out));
  DipSwitch dipswitch (.out(dipswitch_out));
  DipSwitch B0 (.out(multiplier__015_d_1_p6));
  DipSwitch B1 (.out(multiplier__015_d_1_p7));
  DipSwitch B2 (.out(multiplier__015_d_1_p8));
  DipSwitch B3 (.out(multiplier__015_d_1_p9));
  LED X_2 (.in(multiplier__015_d_1_p1));
  LED plus_2 (.in(plus_out));
  LED led (.in(dipswitch_out));
  DDA_4B B (
    .I0(multiplier__015_d_1_p6), .I1(multiplier__015_d_1_p7), .I2(multiplier__015_d_1_p8),
    .I3(multiplier__015_d_1_p9), .O0(B_o0), .O1(B_o1), .O2(B_o2), .O3(B_o3), .T0(B_t0), .T1(B_t1), .T2(B_t2),
    .T3(B_t3));
  _7_segment_driver TB (
    .I3(B_t3), .I2(B_t2), .I1(B_t1), .I0(B_t0), .A(TB_a), .B(TB_b), .C(TB_c), .D(TB_d), .E(TB_e), .F(TB_f),
    .G(TB_g), .H(TB_h));
  Seven_Seg seven_seg_3 (.a(TB_a), .b(TB_b), .c(TB_c), .d(TB_d), .e(TB_e), .f(TB_f), .g(TB_g), .dp(TB_h));
  _7_segment_driver OB (
    .I3(B_o3), .I2(B_o2), .I1(B_o1), .I0(B_o0), .A(OB_a), .B(OB_b), .C(OB_c), .D(OB_d), .E(OB_e), .F(OB_f),
    .G(OB_g), .H(OB_h));
  Seven_Seg seven_seg_4 (.a(OB_a), .b(OB_b), .c(OB_c), .d(OB_d), .e(OB_e), .f(OB_f), .g(OB_g), .dp(OB_h));
  Seven_Seg seven_seg_5 (.a(and_2_out), .b(1'b0), .c(1'b0), .d(and_1_out), .e(1'b0), .f(1'b0), .g(1'b0), .dp(1'b0));
  // OS os_1: pin names not known; wires that end beside it: multiplier__015_d_1_p10, fa_4b_4b_1_s0, fa_4b_4b_2_s0, os_1_p4, os_1_p5, os_1_p6, os_1_p7, os_1_p8, os_1_p9, os_1_p10, os_1_p11
  DDA_8B dda_8b_1 (
    .I7(os_1_p4), .I6(os_1_p5), .I5(os_1_p6), .I4(os_1_p7), .I3(os_1_p8), .I2(os_1_p9), .I1(os_1_p10),
    .I0(os_1_p11), .H3(dda_8b_1_h3), .H2(dda_8b_1_h2), .H1(dda_8b_1_h1), .H0(dda_8b_1_h0), .T3(dda_8b_1_t3),
    .T2(dda_8b_1_t2), .T1(dda_8b_1_t1), .T0(dda_8b_1_t0), .O3(dda_8b_1_o3), .O2(dda_8b_1_o2),
    .O1(dda_8b_1_o1), .O0(dda_8b_1_o0));
  _7_segment_driver H (
    .I3(dda_8b_1_h3), .I2(dda_8b_1_h2), .I1(dda_8b_1_h1), .I0(dda_8b_1_h0), .A(H_a), .B(H_b), .C(H_c),
    .D(H_d), .E(H_e), .F(H_f), .G(H_g), .H(H_h));
  Seven_Seg seven_seg_6 (.a(H_a), .b(H_b), .c(H_c), .d(H_d), .e(H_e), .f(H_f), .g(H_g), .dp(H_h));
  _7_segment_driver T (
    .I3(dda_8b_1_t3), .I2(dda_8b_1_t2), .I1(dda_8b_1_t1), .I0(dda_8b_1_t0), .A(T_a), .B(T_b), .C(T_c),
    .D(T_d), .E(T_e), .F(T_f), .G(T_g), .H(T_h));
  Seven_Seg seven_seg_7 (.a(T_a), .b(T_b), .c(T_c), .d(T_d), .e(T_e), .f(T_f), .g(T_g), .dp(T_h));
  _7_segment_driver O (
    .I3(dda_8b_1_o3), .I2(dda_8b_1_o2), .I1(dda_8b_1_o1), .I0(dda_8b_1_o0), .A(O_a), .B(O_b), .C(O_c),
    .D(O_d), .E(O_e), .F(O_f), .G(O_g), .H(O_h));
  Seven_Seg seven_seg_8 (.a(O_a), .b(O_b), .c(O_c), .d(O_d), .e(O_e), .f(O_f), .g(O_g), .dp(O_h));

  // Notes on the sheet:
  //   A2
  //   A3
  //   B2
  //   B3
  //   A0
  //   A1
  //   B0
  //   B1
  //   T3
  //   T2
  //   T1
  //   T0
  //   C
  //   B
  //   A
  //   E
  //   F
  //   G
  //   H
  //   D
  //   O3
  //   O2
  //   O1
  //   O0
  //   H3
  //   H2
  //   H1
  //   H0
endmodule
