// Digital circuit SEQ 0-7.dig as structural Verilog
module SEQ_0_7 (
  input  clk,
  input  CL,
  input  A,
  input  B,
  input  C,
  input  SET,
  input  X
);

  wire and_1_out, and_2_out, and_3_out, and_4_out, and_5_out, and_6_out, and_7_out, and_8_out, and_9_out,
       and_10_out, not_1_out, not_2_out, not_3_out, not_4_out, or_1_out, or_2_out;

  not not_1 (not_1_out, A);
  not not_2 (not_2_out, B);
  not not_3 (not_3_out, C);
  not not_4 (not_4_out, X);
  and and_1 (and_1_out, B, not_3_out, not_4_out);
  and and_2 (and_2_out, B, C, X);
  and and_3 (and_3_out, not_2_out, not_3_out, not_4_out);
  and and_4 (and_4_out, not_2_out, not_3_out, C);
  and and_5 (and_5_out, not_2_out, C, not_4_out);
  and and_6 (and_6_out, A, not_3_out, not_4_out);
  and and_7 (and_7_out, A, B, X);
  and and_8 (and_8_out, A, not_2_out, C);
  and and_9 (and_9_out, not_1_out, not_2_out, X, not_3_out);
  and and_10 (and_10_out, not_1_out, not_2_out, C, not_4_out);
  or or_1 (or_1_out, and_1_out, and_2_out, and_3_out, and_4_out, and_5_out);
  or or_2 (or_2_out, and_6_out, and_7_out, and_8_out, and_9_out, and_10_out);
  D_FF_AS d_ff_as_1 (.Set(SET), .D(or_2_out), .C(clk), .Clr(CL));  // open: Q, nQ
  D_FF_AS u_B (.Set(SET), .D(or_1_out), .C(clk), .Clr(CL));  // open: Q, nQ
  D_FF_AS u_C (.Set(SET), .D(not_3_out), .C(clk), .Clr(CL));  // open: Q, nQ
endmodule
