// Digital circuit dabble.dig as structural Verilog
module dabble (
  input  I3,
  input  I2,
  input  I1,
  input  I0,
  output O3,
  output O2,
  output O1,
  output O0
);

  wire and_1_out, and_2_out, and_3_out, and_4_out, and_5_out, and_6_out, and_7_out, and_8_out, and_9_out,
       and_10_out, not_1_out, not_2_out, not_3_out, not_4_out;

  not not_1 (not_1_out, I3);
  not not_2 (not_2_out, I2);
  not not_3 (not_3_out, I1);
  not not_4 (not_4_out, I0);
  and and_1 (and_1_out, I3, not_4_out);
  and and_2 (and_2_out, I2, I1, not_4_out);
  and and_3 (and_3_out, not_1_out, not_2_out, I0);
  and and_4 (and_4_out, I1, I0);
  and and_5 (and_5_out, I3, not_4_out);
  and and_6 (and_6_out, not_2_out, I1);
  and and_7 (and_7_out, I2, not_3_out, not_4_out);
  and and_8 (and_8_out, I3, I0);
  and and_9 (and_9_out, I2, I1);
  and and_10 (and_10_out, I2, I0);
  or or_1 (O0, and_1_out, and_2_out, and_3_out);
  or or_2 (O1, and_4_out, and_5_out, and_6_out);
  or or_3 (O2, and_7_out, and_8_out);
  or or_4 (O3, I3, and_9_out, and_10_out);
endmodule
