// Digital circuit test 3.dig as structural Verilog
module test_3 (
);

  wire _7_segment_driver_1_a, _7_segment_driver_1_b, _7_segment_driver_1_c, _7_segment_driver_1_d,
       _7_segment_driver_1_e, _7_segment_driver_1_f, _7_segment_driver_1_g, _7_segment_driver_1_h,
       _7_segment_driver_2_a, _7_segment_driver_2_b, _7_segment_driver_2_c, _7_segment_driver_2_d,
       _7_segment_driver_2_e, _7_segment_driver_2_f, _7_segment_driver_2_g, _7_segment_driver_2_h,
       _7_segment_driver_3_a, _7_segment_driver_3_b, _7_segment_driver_3_c, _7_segment_driver_3_d,
       _7_segment_driver_3_e, _7_segment_driver_3_f, _7_segment_driver_3_g, _7_segment_driver_3_h,
       _7_segment_driver_4_a, _7_segment_driver_4_b, _7_segment_driver_4_c, _7_segment_driver_4_d,
       _7_segment_driver_4_e, _7_segment_driver_4_f, _7_segment_driver_4_g, _7_segment_driver_4_h,
       _7_segment_driver_5_a, _7_segment_driver_5_b, _7_segment_driver_5_c, _7_segment_driver_5_d,
       _7_segment_driver_5_e, _7_segment_driver_5_f, _7_segment_driver_5_g, _7_segment_driver_5_h,
       _7_segment_driver_6_a, _7_segment_driver_6_b, _7_segment_driver_6_c, _7_segment_driver_6_d,
       _7_segment_driver_6_e, _7_segment_driver_6_f, _7_segment_driver_6_g, _7_segment_driver_6_h,
       _7_segment_driver_7_a, _7_segment_driver_7_b, _7_segment_driver_7_c, _7_segment_driver_7_d,
       _7_segment_driver_7_e, _7_segment_driver_7_f, _7_segment_driver_7_g, _7_segment_driver_7_h, A_o0,
       A_o1, A_o2, A_o3, A_t0, A_t1, A_t2, A_t3, and_1_out, and_2_out, B_o0, B_o1, B_o2, B_o3, B_t0, B_t1,
       B_t2, B_t3, dda_8b_1_h0, dda_8b_1_h1, dda_8b_1_h2, dda_8b_1_h3, dda_8b_1_o0, dda_8b_1_o1, dda_8b_1_o2,
       dda_8b_1_o3, dda_8b_1_t0, dda_8b_1_t1, dda_8b_1_t2, dda_8b_1_t3, dipswitch_out,
       multiplier__015_c_1_p1, multiplier__015_c_1_p2, multiplier__015_c_1_p3, multiplier__015_c_1_p4,
       multiplier__015_c_1_p5, multiplier__015_c_1_p6, multiplier__015_c_1_p7, multiplier__015_c_1_p8,
       multiplier__015_c_1_p9, multiplier__015_c_1_p10, or_1_out, os_1_p4, os_1_p5, os_1_p6, os_1_p7,
       os_1_p8, os_1_p9, os_1_p10, os_1_p11, plus_out;
  wire [7:0] fa_4b_4b_1_s0, fa_4b_4b_2_s0;

  or or_1 (or_1_out, dipswitch_out, plus_out, multiplier__015_c_1_p1);
  // Multiplier__015_C multiplier__015_c_1: pin names not known; wires that end beside it: multiplier__015_c_1_p1, multiplier__015_c_1_p2, multiplier__015_c_1_p3, multiplier__015_c_1_p4, multiplier__015_c_1_p5, multiplier__015_c_1_p6, multiplier__015_c_1_p7, multiplier__015_c_1_p8, multiplier__015_c_1_p9, multiplier__015_c_1_p10
  FA_4B_4B fa_4b_4b_1 (
    .En(plus_out), .A0(multiplier__015_c_1_p2), .A1(multiplier__015_c_1_p3), .A2(multiplier__015_c_1_p4),
    .A3(multiplier__015_c_1_p5), .B0(multiplier__015_c_1_p6), .B1(multiplier__015_c_1_p7),
    .B2(multiplier__015_c_1_p8), .B3(multiplier__015_c_1_p9), .S0(fa_4b_4b_1_s0[0]), .S1(fa_4b_4b_1_s0[1]),
    .S2(fa_4b_4b_1_s0[2]), .S3(fa_4b_4b_1_s0[3]), .C4(fa_4b_4b_1_s0[4]), .S5(fa_4b_4b_1_s0[5]),
    .S6(fa_4b_4b_1_s0[6]), .S7(fa_4b_4b_1_s0[7]));
  FA_4B_4B fa_4b_4b_2 (
    .En(dipswitch_out), .A0(multiplier__015_c_1_p2), .A1(multiplier__015_c_1_p3),
    .A2(multiplier__015_c_1_p4), .A3(multiplier__015_c_1_p5), .B0(multiplier__015_c_1_p6),
    .B1(multiplier__015_c_1_p7), .B2(multiplier__015_c_1_p8), .B3(multiplier__015_c_1_p9),
    .S0(fa_4b_4b_2_s0[0]), .S1(fa_4b_4b_2_s0[1]), .S2(fa_4b_4b_2_s0[2]), .S3(fa_4b_4b_2_s0[3]),
    .C4(fa_4b_4b_2_s0[4]), .S5(fa_4b_4b_2_s0[5]), .S6(fa_4b_4b_2_s0[6]), .S7(fa_4b_4b_2_s0[7]));
  DDA_4B A (
    .I0(multiplier__015_c_1_p2), .I1(multiplier__015_c_1_p3), .I2(multiplier__015_c_1_p4),
    .I3(multiplier__015_c_1_p5), .O0(A_o0), .O1(A_o1), .O2(A_o2), .O3(A_o3), .T0(A_t0), .T1(A_t1), .T2(A_t2),
    .T3(A_t3));
  and and_1 (and_1_out, 1'b1, or_1_out);
  and and_2 (and_2_out, 1'b1, or_1_out);
  _7_segment_driver _7_segment_driver_1 (
    .I3(A_t3), .I2(A_t2), .I1(A_t1), .I0(A_t0), .A(_7_segment_driver_1_a), .B(_7_segment_driver_1_b),
    .C(_7_segment_driver_1_c), .D(_7_segment_driver_1_d), .E(_7_segment_driver_1_e),
    .F(_7_segment_driver_1_f), .G(_7_segment_driver_1_g), .H(_7_segment_driver_1_h));
  Seven_Seg seven_seg_1 (
    .a(_7_segment_driver_1_a), .b(_7_segment_driver_1_b), .c(_7_segment_driver_1_c),
    .d(_7_segment_driver_1_d), .e(_7_segment_driver_1_e), .f(_7_segment_driver_1_f),
    .g(_7_segment_driver_1_g), .dp(_7_segment_driver_1_h));
  _7_segment_driver _7_segment_driver_2 (
    .I3(A_o3), .I2(A_o2), .I1(A_o1), .I0(A_o0), .A(_7_segment_driver_2_a), .B(_7_segment_driver_2_b),
    .C(_7_segment_driver_2_c), .D(_7_segment_driver_2_d), .E(_7_segment_driver_2_e),
    .F(_7_segment_driver_2_f), .G(_7_segment_driver_2_g), .H(_7_segment_driver_2_h));
  Seven_Seg seven_seg_2 (
    .a(_7_segment_driver_2_a), .b(_7_segment_driver_2_b), .c(_7_segment_driver_2_c),
    .d(_7_segment_driver_2_d), .e(_7_segment_driver_2_e), .f(_7_segment_driver_2_f),
    .g(_7_segment_driver_2_g), .dp(_7_segment_driver_2_h));
  DipSwitch A0 (.out(multiplier__015_c_1_p2));
  DipSwitch A1 (.out(multiplier__015_c_1_p3));
  DipSwitch A2 (.out(multiplier__015_c_1_p4));
  DipSwitch A3 (.out(multiplier__015_c_1_p5));
  DipSwitch X (.out(multiplier__015_c_1_p1));
  DipSwitch plus (.out(plus_out));
  DipSwitch dipswitch (.out(dipswitch_out));
  DipSwitch B0 (.out(multiplier__015_c_1_p6));
  DipSwitch B1 (.out(multiplier__015_c_1_p7));
  DipSwitch B2 (.out(multiplier__015_c_1_p8));
  DipSwitch B3 (.out(multiplier__015_c_1_p9));
  LED X_2 (.in(multiplier__015_c_1_p1));
  LED plus_2 (.in(plus_out));
  LED led (.in(dipswitch_out));
  DDA_4B B (
    .I0(multiplier__015_c_1_p6), .I1(multiplier__015_c_1_p7), .I2(multiplier__015_c_1_p8),
    .I3(multiplier__015_c_1_p9), .O0(B_o0), .O1(B_o1), .O2(B_o2), .O3(B_o3), .T0(B_t0), .T1(B_t1), .T2(B_t2),
    .T3(B_t3));
  _7_segment_driver _7_segment_driver_3 (
    .I3(B_t3), .I2(B_t2), .I1(B_t1), .I0(B_t0), .A(_7_segment_driver_3_a), .B(_7_segment_driver_3_b),
    .C(_7_segment_driver_3_c), .D(_7_segment_driver_3_d), .E(_7_segment_driver_3_e),
    .F(_7_segment_driver_3_f), .G(_7_segment_driver_3_g), .H(_7_segment_driver_3_h));
  Seven_Seg seven_seg_3 (
    .a(_7_segment_driver_3_a), .b(_7_segment_driver_3_b), .c(_7_segment_driver_3_c),
    .d(_7_segment_driver_3_d), .e(_7_segment_driver_3_e), .f(_7_segment_driver_3_f),
    .g(_7_segment_driver_3_g), .dp(_7_segment_driver_3_h));
  _7_segment_driver _7_segment_driver_4 (
    .I3(B_o3), .I2(B_o2), .I1(B_o1), .I0(B_o0), .A(_7_segment_driver_4_a), .B(_7_segment_driver_4_b),
    .C(_7_segment_driver_4_c), .D(_7_segment_driver_4_d), .E(_7_segment_driver_4_e),
    .F(_7_segment_driver_4_f), .G(_7_segment_driver_4_g), .H(_7_segment_driver_4_h));
  Seven_Seg seven_seg_4 (
    .a(_7_segment_driver_4_a), .b(_7_segment_driver_4_b), .c(_7_segment_driver_4_c),
    .d(_7_segment_driver_4_d), .e(_7_segment_driver_4_e), .f(_7_segment_driver_4_f),
    .g(_7_segment_driver_4_g), .dp(_7_segment_driver_4_h));
  Seven_Seg seven_seg_5 (.a(and_2_out), .b(1'b0), .c(1'b0), .d(and_1_out), .e(1'b0), .f(1'b0), .g(1'b0), .dp(1'b0));
  // OS os_1: pin names not known; wires that end beside it: multiplier__015_c_1_p10, fa_4b_4b_1_s0, fa_4b_4b_2_s0, os_1_p4, os_1_p5, os_1_p6, os_1_p7, os_1_p8, os_1_p9, os_1_p10, os_1_p11
  DDA_8B dda_8b_1 (
    .I7(os_1_p4), .I6(os_1_p5), .I5(os_1_p6), .I4(os_1_p7), .I3(os_1_p8), .I2(os_1_p9), .I1(os_1_p10),
    .I0(os_1_p11), .H3(dda_8b_1_h3), .H2(dda_8b_1_h2), .H1(dda_8b_1_h1), .H0(dda_8b_1_h0), .T3(dda_8b_1_t3),
    .T2(dda_8b_1_t2), .T1(dda_8b_1_t1), .T0(dda_8b_1_t0), .O3(dda_8b_1_o3), .O2(dda_8b_1_o2),
    .O1(dda_8b_1_o1), .O0(dda_8b_1_o0));
  _7_segment_driver _7_segment_driver_5 (
    .I3(dda_8b_1_h3), .I2(dda_8b_1_h2), .I1(dda_8b_1_h1), .I0(dda_8b_1_h0), .A(_7_segment_driver_5_a),
    .B(_7_segment_driver_5_b), .C(_7_segment_driver_5_c), .D(_7_segment_driver_5_d),
    .E(_7_segment_driver_5_e), .F(_7_segment_driver_5_f), .G(_7_segment_driver_5_g), .H(_7_segment_driver_5_h));
  Seven_Seg seven_seg_6 (
    .a(_7_segment_driver_5_a), .b(_7_segment_driver_5_b), .c(_7_segment_driver_5_c),
    .d(_7_segment_driver_5_d), .e(_7_segment_driver_5_e), .f(_7_segment_driver_5_f),
    .g(_7_segment_driver_5_g), .dp(_7_segment_driver_5_h));
  _7_segment_driver _7_segment_driver_6 (
    .I3(dda_8b_1_t3), .I2(dda_8b_1_t2), .I1(dda_8b_1_t1), .I0(dda_8b_1_t0), .A(_7_segment_driver_6_a),
    .B(_7_segment_driver_6_b), .C(_7_segment_driver_6_c), .D(_7_segment_driver_6_d),
    .E(_7_segment_driver_6_e), .F(_7_segment_driver_6_f), .G(_7_segment_driver_6_g), .H(_7_segment_driver_6_h));
  Seven_Seg seven_seg_7 (
    .a(_7_segment_driver_6_a), .b(_7_segment_driver_6_b), .c(_7_segment_driver_6_c),
    .d(_7_segment_driver_6_d), .e(_7_segment_driver_6_e), .f(_7_segment_driver_6_f),
    .g(_7_segment_driver_6_g), .dp(_7_segment_driver_6_h));
  _7_segment_driver _7_segment_driver_7 (
    .I3(dda_8b_1_o3), .I2(dda_8b_1_o2), .I1(dda_8b_1_o1), .I0(dda_8b_1_o0), .A(_7_segment_driver_7_a),
    .B(_7_segment_driver_7_b), .C(_7_segment_driver_7_c), .D(_7_segment_driver_7_d),
    .E(_7_segment_driver_7_e), .F(_7_segment_driver_7_f), .G(_7_segment_driver_7_g), .H(_7_segment_driver_7_h));
  Seven_Seg seven_seg_8 (
    .a(_7_segment_driver_7_a), .b(_7_segment_driver_7_b), .c(_7_segment_driver_7_c),
    .d(_7_segment_driver_7_d), .e(_7_segment_driver_7_e), .f(_7_segment_driver_7_f),
    .g(_7_segment_driver_7_g), .dp(_7_segment_driver_7_h));

  // Notes on the sheet:
  //   A3
  //   B3
  //   A1
  //   A2
  //   B1
  //   B2
  //   A0
  //   B0
  //   T3
  //   T2
  //   T1
  //   T0
  //   E
  //   D
  //   C
  //   B
  //   A
  //   F
  //   G
  //   H
  //   O3
  //   O2
  //   O1
  //   O0
  //   H3
  //   H2
  //   H1
  //   H0
endmodule
